// Digital circuit fac.dig as structural Verilog
module fac (
  input  y,
  input  x,
  input  c_in,
  output z,
  output c_out
);

  wire and_1_out, and_2_out, and_3_out;

  or or_1 (c_out, and_3_out, and_2_out, and_1_out);
  and and_1 (and_1_out, x, c_in);
  and and_2 (and_2_out, y, c_in);
  and and_3 (and_3_out, y, x);
  xor xor_1 (z, y, x, c_in);
endmodule
